// Logisim project Regfile.circ as structural Verilog: 1 circuit, main circuit main
module main (
  input  [1:0] Read_register_1,
  input  [1:0] Read_register_2,
  input  [1:0] write_register,
  input  [15:0] write_data,
  input  RegWrite,
  input  clock,
  output [15:0] Reg_0_Value,
  output [15:0] Reg_1_Value,
  output [15:0] Reg_2_Value,
  output [15:0] Reg_3_Value,
  output [15:0] Read_Data_1,
  output [15:0] Read_Data_2
);

  wire Write0, Write1, Write2, Write3;

  Register #(.width(16)) Reg0 (.D(write_data), .en(Write0), .Q(Reg_0_Value), .clk(clock));  // open: clr
  Demultiplexer #(.select(2)) demultiplexer_1 (
    .out0(Write0), .out1(Write1), .out2(Write2), .out3(Write3), .in(RegWrite), .sel(write_register));  // open: en
  Register #(.width(16)) Reg1 (.D(write_data), .en(Write1), .Q(Reg_1_Value), .clk(clock));  // open: clr
  Register #(.width(16)) Reg2 (.D(write_data), .en(Write2), .Q(Reg_2_Value), .clk(clock));  // open: clr
  Register #(.width(16)) Reg3 (.D(write_data), .en(Write3), .Q(Reg_3_Value), .clk(clock));  // open: clr
  Multiplexer #(.select(2), .width(16)) multiplexer_1 (
    .in0(Reg_0_Value), .in1(Reg_1_Value), .in2(Reg_2_Value), .in3(Reg_3_Value), .out(Read_Data_1),
    .sel(Read_register_1));  // open: en
  Multiplexer #(.select(2), .width(16)) multiplexer_2 (
    .in0(Reg_0_Value), .in1(Reg_1_Value), .in2(Reg_2_Value), .in3(Reg_3_Value), .out(Read_Data_2),
    .sel(Read_register_2));  // open: en

  // Other names for the same wires on the sheet: Clk = clock; Data[15:0] = write_data; Read1[1:0] = Read_register_1;
  //   Read2[1:0] = Read_register_2; Reg0[15:0] = Reg_0_Value; Reg1[15:0] = Reg_1_Value; Reg2[15:0] = Reg_2_Value;
  //   Reg3[15:0] = Reg_3_Value

  // Notes on the sheet:
  //   These are INPUTS to the circuit
  //   These are INPUTS to the circuit
  //   DO NOT CHANGE THE LOCATIONS OF THE INPUTS/OUTPUTS! IF YOU DO SO, YOU NEED TO MAKE SURE THE PINS ARE AT THE RIGHT PLACE!
  //   These are OUTPUTS to the circuit
  //   Yet again, the clock is not an actual clock, but an input, one that will be driven from a higher circuit
  //   These are OUTPUTS to the circuit
endmodule
