// Logisim project alu.circ as structural Verilog: 4 circuits, main circuit main
module main (
  input  [15:0] X,
  input  [15:0] Y,
  input  [3:0] Switch__S,
  output Signed_Overflow,
  output [15:0] RESULT,
  output Equal
);

  wire overflow_1_add_overflow, overflow_1_addp8_overflow, overflow_1_sub_overflow, overflow_1_subp8_overflow;
  wire [0:0] comparator_1_lt;
  wire [15:0] adder_1_out, addp8_1_out, and_1_out, or_1_out, shifter_1_out, shifter_2_out, shifter_3_out,
       shifter_4_out, subp8_1_out, subtractor_1_out;

  Adder #(.width(16)) adder_1 (.a(X), .b(Y), .out(adder_1_out));  // open: cin, cout
  Subtractor #(.width(16)) subtractor_1 (.a(X), .b(Y), .out(subtractor_1_out));  // open: bin, bout
  Shifter #(.width(16)) shifter_1 (.in(X), .\dist (Y[3:0]), .out(shifter_1_out));
  Shifter #(.width(16), .shift("lr")) shifter_2 (.in(X), .\dist (Y[3:0]), .out(shifter_2_out));
  Shifter #(.width(16), .shift("ar")) shifter_3 (.in(X), .\dist (Y[3:0]), .out(shifter_3_out));
  Comparator #(.width(16)) comparator_1 (.a(X), .b(Y), .lt(comparator_1_lt[0]));  // open: gt, eq
  assign or_1_out = X | Y;  // OR_Gate or_1, 16 bits wide
  assign and_1_out = X & Y;  // AND_Gate and_1, 16 bits wide
  addp8 addp8_1 (.Input_X(X), .Input_Y(Y), .out(addp8_1_out));
  subp8 subp8_1 (.Input_X(X), .Input_Y(Y), .out(subp8_1_out));
  Shifter #(.width(16)) shifter_4 (.in(Y), .\dist (4'b1000), .out(shifter_4_out));
  Multiplexer #(.select(4), .width(16)) multiplexer_1 (
    .in0(adder_1_out), .in1(subtractor_1_out), .in2(shifter_1_out), .in3(shifter_2_out), .in4(shifter_3_out),
    .in5({{15{1'b0}}, comparator_1_lt[0]}), .in6(or_1_out), .in7(and_1_out), .in8(addp8_1_out),
    .in9(subp8_1_out), .in10(shifter_4_out), .out(RESULT), .sel(Switch__S));  // open: in11, in12, in13, in14, in15, en
  Overflow overflow_1 (
    .Input_X(X), .Input_Y(Y), .Result(RESULT), .Add_Overflow(overflow_1_add_overflow),
    .Sub_Overflow(overflow_1_sub_overflow), .Addp8_Overflow(overflow_1_addp8_overflow),
    .Subp8_Overflow(overflow_1_subp8_overflow));
  Comparator #(.width(16)) comparator_2 (.a(X), .b(Y), .eq(Equal));  // open: gt, lt
  Multiplexer #(.select(4)) multiplexer_2 (
    .in0(overflow_1_add_overflow), .in1(overflow_1_sub_overflow), .in2(1'b0), .in3(1'b0), .in4(1'b0),
    .in5(1'b0), .in6(1'b0), .in7(1'b0), .in8(overflow_1_addp8_overflow), .in9(overflow_1_subp8_overflow),
    .in10(1'b0), .in11(1'b0), .in12(1'b0), .in13(1'b0), .in14(1'b0), .in15(1'b0), .out(Signed_Overflow),
    .sel(Switch__S));  // open: en

  // Other names for the same wires on the sheet: Overflow = Signed_Overflow; Select[3:0] = Switch__S

  // Notes on the sheet:
  //   INPUTS to your circuit
  //   INPUT to your circuit
  //   sllv
  //   srvl
  //   srav
  //   addp8
  //   subp8
  //   lui(only for cpu)
  //   add
  //   sub
  //   slt
  //   or
  //   and
  //   DON'T CHANGE THE INPUTS AND OUTPUTS! IF YOU DO SO, YOU NEED TO MAKE SURE THE PINS ARE IN THE RIGHT PLACES!
  //   OUTPUTS of your circuit
endmodule

module addp8 (
  input  [15:0] Input_X,
  input  [15:0] Input_Y,
  output [15:0] out
);

  Adder adder_1 (.a(Input_X[7:0]), .b(Input_Y[7:0]), .out(out[7:0]));  // open: cin, cout
  Adder adder_2 (.a(Input_X[15:8]), .b(Input_Y[15:8]), .out(out[15:8]));  // open: cin, cout
endmodule

module subp8 (
  input  [15:0] Input_X,
  input  [15:0] Input_Y,
  output [15:0] out
);

  Subtractor subtractor_1 (.a(Input_X[7:0]), .b(Input_Y[7:0]), .out(out[7:0]));  // open: bin, bout
  Subtractor subtractor_2 (.a(Input_X[15:8]), .b(Input_Y[15:8]), .out(out[15:8]));  // open: bin, bout
endmodule

module Overflow (
  input  [15:0] Input_X,
  input  [15:0] Input_Y,
  input  [15:0] Result,
  output Add_Overflow,
  output Sub_Overflow,
  output Addp8_Overflow,
  output Subp8_Overflow
);

  wire and_1_out, and_2_out, and_3_out, and_4_out, and_5_out, and_6_out, and_7_out, and_8_out, and_9_out,
       multiplexer_3_out, multiplexer_4_out, multiplexer_5_out, multiplexer_6_out, nor_1_out, nor_2_out,
       nor_3_out, not_1_out, not_2_out, not_3_out, not_4_out, not_5_out, not_6_out;

  and and_1 (and_1_out, Input_X[15], Input_Y[15]);
  nor nor_1 (nor_1_out, Input_X[15], Input_Y[15]);
  not not_1 (not_1_out, Input_Y[15]);
  not not_2 (not_2_out, Input_X[15]);
  and and_2 (and_2_out, Input_X[15], Input_Y[15]);
  nor nor_2 (nor_2_out, Input_X[15], Input_Y[15]);
  and and_3 (and_3_out, Input_X[7], Input_Y[7]);
  nor nor_3 (nor_3_out, Input_X[7], Input_Y[7]);
  not not_3 (not_3_out, Input_Y[15]);
  not not_4 (not_4_out, Input_X[15]);
  not not_5 (not_5_out, Input_Y[7]);
  not not_6 (not_6_out, Input_X[7]);
  Multiplexer multiplexer_1 (.in0(and_1_out), .in1(nor_1_out), .out(Add_Overflow), .sel(Result[15]));  // open: en
  and and_4 (and_4_out, Input_X[15], not_1_out);
  Multiplexer multiplexer_2 (.in0(and_4_out), .in1(and_5_out), .out(Sub_Overflow), .sel(Result[15]));  // open: en
  and and_5 (and_5_out, not_2_out, Input_Y[15]);
  Multiplexer multiplexer_3 (.in0(and_2_out), .in1(nor_2_out), .out(multiplexer_3_out), .sel(Result[15]));  // open: en
  Multiplexer multiplexer_4 (.in0(and_3_out), .in1(nor_3_out), .out(multiplexer_4_out), .sel(Result[7]));  // open: en
  and and_6 (and_6_out, Input_X[15], not_3_out);
  Multiplexer multiplexer_5 (.in0(and_6_out), .in1(and_7_out), .out(multiplexer_5_out), .sel(Result[15]));  // open: en
  and and_7 (and_7_out, not_4_out, Input_Y[15]);
  and and_8 (and_8_out, Input_X[7], not_5_out);
  Multiplexer multiplexer_6 (.in0(and_8_out), .in1(and_9_out), .out(multiplexer_6_out), .sel(Result[7]));  // open: en
  and and_9 (and_9_out, not_6_out, Input_Y[7]);
  or or_1 (Addp8_Overflow, multiplexer_3_out, multiplexer_4_out);
  or or_2 (Subp8_Overflow, multiplexer_5_out, multiplexer_6_out);

  // Other names for the same wires on the sheet: Sign_X1 = Input_X[7]; Sign_X = Input_X[15]; Sign_Y1 = Input_Y[7];
  //   Sign_Y = Input_Y[15]; Sign_Result1 = Result[7]; Sign_Result = Result[15]
endmodule
