// Logisim project cpu.circ as structural Verilog: 1 circuit, main circuit main
module main (
  input  [15:0] From_Instr_Mem,
  input  clk,
  input  in_3,
  output [15:0] r0,
  output [15:0] r1,
  output [15:0] r2,
  output [15:0] r3,
  output [15:0] Display_0,
  output [15:0] Display_1,
  output [15:0] To_Instr_Mem,
  output [15:0] Data_Mem_Data,
  output [15:0] Data_Mem_Addr,
  output Data_Mem_Write
);

  wire ADDI, and_1_out, and_2_out, and_4_out, and_5_out, ANDI, BEQ, BNE, Branch, comparator_1_eq,
       comparator_2_eq, DISP, Equal, J, JAL, JR, Jump_Instr, Kill, LUI, LW, main_2_signed_overflow,
       not_1_out, not_2_out, ORI, R_TYPE, RegWr, Sign_Unsigned, Use_Imm;
  wire [1:0] multiplexer_4_out, multiplexer_5_out;
  wire [3:0] Function, multiplexer_9_out, Non_R_Switch, opcode;
  wire [11:4] Jump_Address;
  wire [15:0] adder_1_out, adder_2_out, and_3_out, bit_extender_1_out, bit_extender_3_out, Datain, DataWr,
       DataWr_Final, Imm, Jump_Target, multiplexer_1_out, multiplexer_2_out, multiplexer_3_out,
       multiplexer_8_out, multiplexer_10_out, multiplexer_12_out, or_7_out, RS, undriven;

  Multiplexer #(.width(16), .enable("false")) multiplexer_1 (
    .in0(multiplexer_2_out), .in1(Jump_Target), .out(multiplexer_1_out), .sel(Jump_Instr));
  Register #(.width(16)) PC (.D(multiplexer_1_out), .Q(To_Instr_Mem), .clk(clk));  // open: en, clr
  or or_1 (Sign_Unsigned, BEQ, ADDI, BNE, Data_Mem_Write, LW);
  and and_1 (and_1_out, BEQ, Equal);
  not not_1 (not_1_out, Equal);
  Adder #(.width(16)) adder_1 (.a(To_Instr_Mem), .b(16'h1), .out(adder_1_out));  // open: cin, cout
  or or_2 (Kill, Jump_Instr, Branch);
  and and_2 (and_2_out, not_1_out, BNE);
  Multiplexer #(.width(16), .enable("false")) multiplexer_2 (
    .in0(adder_1_out), .in1(adder_2_out), .out(multiplexer_2_out), .sel(Branch));
  Multiplexer #(.width(16), .enable("false")) multiplexer_3 (
    .in0(From_Instr_Mem), .in1(16'h6), .out(multiplexer_3_out), .sel(Kill));
  or or_3 (Branch, and_1_out, and_2_out);
  Adder #(.width(16)) adder_2 (.a(To_Instr_Mem), .b(Imm), .out(adder_2_out));  // open: cin, cout
  Register #(.width(16)) register_1 (
    .D(multiplexer_3_out), .Q({opcode, Jump_Address, Function}), .clk(clk), .clr(clk));  // open: en
  Demultiplexer #(.select(4), .enable("false")) demultiplexer_1 (
    .out0(R_TYPE), .out1(JAL), .out2(J), .out3(JR), .out4(BEQ), .out5(ADDI), .out6(ANDI), .out7(ORI),
    .out8(BNE), .out9(Data_Mem_Write), .out10(LUI), .out11(LW), .out12(DISP), .in(1'b1), .sel(opcode));  // open: out13, out14, out15
  Multiplexer #(.width(2), .enable("false")) multiplexer_4 (
    .in0(Jump_Address[9:8]), .in1(Jump_Address[7:6]), .out(multiplexer_4_out), .sel(R_TYPE));
  assign bit_extender_1_out = {{8{1'b0}}, {Jump_Address[7:4], Function}};  // Bit_Extender bit_extender_1
  Bit_Extender #(.\type ("sign")) bit_extender_2 ();  // open: in, out
  or or_4 (Jump_Instr, JAL, J, JR);
  Multiplexer #(.width(2), .enable("false")) multiplexer_5 (
    .in0(multiplexer_4_out), .in1(2'b11), .out(multiplexer_5_out), .sel(JAL));
  Multiplexer #(.width(16)) multiplexer_6 (
    .in0(bit_extender_1_out), .in1(undriven), .out(Imm), .sel(Sign_Unsigned));  // open: en
  or or_5 (Use_Imm, Jump_Instr, BEQ, ADDI, ORI, BNE, Data_Mem_Write, LUI, LW, DISP, ANDI);
  // Regfile_main main_1: pin names not known; wires that end beside it: Jump_Address[11:10], Jump_Address[9:8], multiplexer_5_out, DataWr_Final, r0, r1, RegWr, r2, clk, r3, RS, Datain
  or or_6 (RegWr, ADDI, ANDI, ORI, LUI, LW, R_TYPE);
  Multiplexer #(.width(16), .enable("false")) multiplexer_7 (
    .in0(DataWr), .in1(To_Instr_Mem), .out(DataWr_Final), .sel(JAL));
  Multiplexer #(.width(16), .enable("false")) multiplexer_8 (
    .in0(Datain), .in1(Imm), .out(multiplexer_8_out), .sel(Use_Imm));
  assign bit_extender_3_out = {{4{1'b0}}, {Jump_Address, Function}};  // Bit_Extender bit_extender_3
  assign and_3_out = To_Instr_Mem & 16'hf000;  // AND_Gate and_3, 16 bits wide
  Hex_Digit_Display hex_digit_display_1 (.value(Display_0[15:12]));  // open: dp
  alu_main main_2 (
    .Switch__S(multiplexer_9_out), .X(RS), .Equal(Equal), .RESULT(Data_Mem_Addr),
    .Signed_Overflow(main_2_signed_overflow), .Y(multiplexer_8_out));
  Multiplexer #(.width(4)) multiplexer_9 (
    .in0(Non_R_Switch), .in1(Function), .out(multiplexer_9_out), .sel(R_TYPE));  // open: en
  assign or_7_out = bit_extender_3_out | and_3_out;  // OR_Gate or_7, 16 bits wide
  Hex_Digit_Display hex_digit_display_2 (.value(Display_0[11:8]));  // open: dp
  Hex_Digit_Display hex_digit_display_3 (.value(Display_0[7:4]));  // open: dp
  Multiplexer #(.width(16), .enable("false")) multiplexer_10 (
    .in0(Display_0), .in1(RS), .out(multiplexer_10_out), .sel(and_4_out));
  and and_4 (and_4_out, comparator_1_eq, DISP);
  Comparator #(.width(16)) comparator_1 (.a({16{1'b0}}), .b(Imm), .eq(comparator_1_eq));  // open: gt, lt
  LED led_1 (.in(main_2_signed_overflow));
  Multiplexer #(.width(16), .enable("false")) multiplexer_11 (.in0(or_7_out), .in1(RS), .out(Jump_Target), .sel(JR));
  Hex_Digit_Display hex_digit_display_4 (.value(Display_0[3:0]));  // open: dp
  Register #(.width(16)) register_2 (.D(multiplexer_10_out), .Q(Display_0), .clk(clk));  // open: en, clr
  Hex_Digit_Display hex_digit_display_5 (.value(Display_1[11:8]));  // open: dp
  Hex_Digit_Display hex_digit_display_6 (.value(Display_1[15:12]));  // open: dp
  Hex_Digit_Display hex_digit_display_7 (.value(Display_1[7:4]));  // open: dp
  Multiplexer #(.width(16), .enable("false")) multiplexer_12 (
    .in0(Display_1), .in1(RS), .out(multiplexer_12_out), .sel(and_5_out));
  and and_5 (and_5_out, comparator_2_eq, DISP);
  Comparator #(.width(16)) comparator_2 (.a(16'h1), .b(Imm), .eq(comparator_2_eq));  // open: gt, lt
  Multiplexer #(.select(4), .width(4), .enable("false")) multiplexer_13 (
    .in5(4'b0000), .in6(4'b0111), .in7(4'b0110), .in9(4'b0000), .in10(4'b1010), .in11(4'b0000),
    .out(Non_R_Switch), .sel(opcode));  // open: in0, in1, in2, in3, in4, in8, in12, in13, in14, in15
  assign Data_Mem_Data = Data_Mem_Write ? Datain : 16'bz;  // Controlled_Buffer controlled_buffer_1
  RAM #(.addrWidth(16), .dataWidth(16)) ram_1 (
    .addr(Data_Mem_Addr), .data(Data_Mem_Data), .sel(1'b1), .clk(clk), .ld(not_2_out), .clr(in_3));
  not not_2 (not_2_out, Data_Mem_Write);
  Hex_Digit_Display hex_digit_display_8 (.value(Display_1[3:0]));  // open: dp
  Register #(.width(16)) register_3 (.D(multiplexer_12_out), .Q(Display_1), .clk(clk));  // open: en, clr
  Multiplexer #(.width(16), .enable("false")) multiplexer_14 (
    .in0(Data_Mem_Addr), .in1(Data_Mem_Data), .out(DataWr), .sel(LW));

  // Other names for the same wires on the sheet: Jump_Address[3:0] = Function; ALU_OUT[15:0] = Data_Mem_Addr;
  //   Current_PC[15:0] = To_Instr_Mem; d0[15:0] = Display_0; d1[15:0] = Display_1; Data_Out[15:0] = Data_Mem_Data;
  //   Mem_to_Reg = LW; RT[15:0] = Datain; MemWr = Data_Mem_Write; SW = Data_Mem_Write

  // Notes on the sheet:
  //   This is the current PC that you need to send as OUTPUT
  //   This is the instruction that you would receive as INPUT
  //   PROGRAM COUNTER
  //   SIGNED/UNSIGNED + MEM WRITE AND MEM TO REG
  //   BRANCHING
  //   This is a CLK that is an INPUT driven from the harness.
  //   Remember, this circuit is loaded from the harness to be tested!
  //   DO NOT CHANGE THE LOCATIONS OF THE INPUTS OR OUTPUTS! IF YOU DO SO, YOU NEED TO MAKE SURE THE PINS ARE IN THE RIGHT PLACES!
  //   These are OUTPUTS of the circuit
  //   INSTRUCTIONS
  //   USE IMMEDIATE?
  //   REGISTER FILE
  //   IMMEDIATE HANDLING
  //   WRITE TO REG
  //   OUTPUT
  //   WRITE TO DATA
  //   ALU
  //   These are OUTPUTS of the circuit
  //   JUMPING
  //   DISPLAY/OUTPUT DEVICE
  //   NON-R SWITCH
  //   DATA MEMORY
endmodule
